// Logisim project second_task.circ as structural Verilog: 1 circuit, main circuit main
module main (
  input  x4,
  input  x3,
  input  x2,
  input  x1,
  output y4,
  output y3,
  output y2,
  output y1
);

  wire and_1_out, and_2_out, and_3_out, and_4_out, and_5_out, and_6_out, not_1_out;

  not not_1 (not_1_out, x4);
  not not_2 (y3, x3);
  and and_1 (and_1_out, not_1_out, x3);
  and and_2 (and_2_out, x4, y3);
  and and_3 (and_3_out, x2, not_1_out);
  and and_4 (and_4_out, x2, y3);
  and and_5 (and_5_out, x1, not_1_out);
  and and_6 (and_6_out, x1, y3);
  or or_1 (y4, and_1_out, and_2_out);
  or or_2 (y2, and_3_out, and_4_out);
  or or_3 (y1, and_5_out, and_6_out);
endmodule
